# Fritzing sketch 74hc595 (saved by Fritzing 0.9.5d)
breadboards: 1

parts:
  U1 = 74HC595 [package="DIP16 [THT]"]
  U2 = 74HC595 [package="DIP16 [THT]"]
  Raspberry_Pi_1 = Raspberry Pi 3 [part_number=RPI-3-V1.2]

nets:
  GND: U1.GND, U1.OE, U2.GND, U2.OE, Raspberry_Pi_1.GND
  N1: U1.Q7', U2.DS
  VCC: U1.MR, U1.VCC, U2.MR, U2.VCC, Raspberry_Pi_1.3v3
  N2: U1.SH_CP, U2.SH_CP, Raspberry_Pi_1.GPIO5
  N3: U1.ST_CP, Raspberry_Pi_1.GPIO6
  N4: U1.DS, Raspberry_Pi_1.GPIO16
