# Fritzing sketch Ejer_2_Ojitos (saved by Fritzing 0.9.5d)
breadboards: 1

parts:
  Raspberry_Pi_1 = Raspberry Pi 3 [part_number=RPI-3-V1.2]
  R1 = Resistor [tolerance=±2% resistance=1000 package="1206 [SMD]"]
  R2 = Resistor [tolerance=±2% resistance=2000 package="1206 [SMD]"]
  HC-SR04_Sensor_1 = HC-SR04 Ultrasonic Distance Sensor

nets:
  GND: Raspberry_Pi_1.GND, R2.Pin_1, HC-SR04_Sensor_1.GND
  N1: Raspberry_Pi_1.GPIO24, R1.Pin_1, R2.Pin_0
  N2: Raspberry_Pi_1.GPIO23, HC-SR04_Sensor_1.TRIG
  5V: Raspberry_Pi_1.5V, HC-SR04_Sensor_1.VCC
  N3: R1.Pin_0, HC-SR04_Sensor_1.ECHO
