# Fritzing sketch Ejer_4_LCD02 (saved by Fritzing 0.9.5d)
breadboards: 1

parts:
  U2 = LCD-16X2 [package=lcd-16x2_nosilk]
  Raspberry_Pi_1 = Raspberry Pi 3 [part_number=RPI-3-V1.2]
  U3 = POT [package=pot_alpha_rv16af-20]

nets:
  VSS: U2.VSS, U2.RS, U2.K, Raspberry_Pi_1.GND, U3.E
  VDD: U2.VDD, U2.A, Raspberry_Pi_1.5V, U3.A
  N1: U2.VO, U3.S
  N2: U2.R_W, Raspberry_Pi_1.GIPO18
  N3: U2.DB4, Raspberry_Pi_1.GIPO27
  N4: U2.DB5, Raspberry_Pi_1.GIPO22
  N5: U2.DB6, Raspberry_Pi_1.GIPO23
  N6: U2.DB7, Raspberry_Pi_1.GIPO24
