# Fritzing sketch Exercici4Full (saved by Fritzing 0.9.5d)
breadboards: 1

parts:
  Raspberry_Pi_1 = Raspberry Pi 3 [part_number=RPI-3-V1.2]
  HC-SR04_Sensor_1 = HC-SR04 Ultrasonic Distance Sensor
  R1 = Resistor [tolerance=±5% resistance=1k package="0805 [SMD]"]
  R2 = Resistor [tolerance=±5% resistance=2.2k package="2010 [SMD]"]
  R3 = Resistor [tolerance=±5% resistance=220 package="1206 [SMD]"]
  LED1 = smd LED [color="Green (555nm)" package="0603 [SMD]"]
  buz1 = Piezo Buzzer  # not connected

nets:
  N1: Raspberry_Pi_1.GPIO17, R3.Pin_0
  N2: Raspberry_Pi_1.GPIO24, R1.Pin_1, R2.Pin_0
  N3: Raspberry_Pi_1.GPIO23, HC-SR04_Sensor_1.TRIG
  5V: Raspberry_Pi_1.5V, HC-SR04_Sensor_1.VCC
  N4: HC-SR04_Sensor_1.ECHO, R1.Pin_0
  N5: HC-SR04_Sensor_1.GND, R2.Pin_1, LED1.cathode
  N6: R3.Pin_1, LED1.anode

custom parts:
  Piezo Buzzer: Part from https://www.nutsvolts.com/magazine/article/november2012_SmileysWorkshop. Breadboard and icon images modified to be 0.3" in spacing and be more similar to the actual physical part.
