# Fritzing sketch Exercici6Full (saved by Fritzing 0.9.5d)
breadboards: 1

parts:
  Raspberry_Pi_1 = Raspberry Pi 3 [part_number=RPI-3-V1.2]
  HC-SR04_Sensor_1 = HC-SR04 Ultrasonic Distance Sensor
  R1 = Resistor [tolerance=±5% resistance=1k package="0805 [SMD]"]
  R2 = Resistor [tolerance=±5% resistance=2.2k package="2010 [SMD]"]
  R3 = Resistor [tolerance=±5% resistance=220 package="1206 [SMD]"]
  LED1 = smd LED [color="Blue (430nm)" package="0603 [SMD]"]
  LED2 = smd LED [color="Red (635nm)" package="0603 [SMD]"]
  LED3 = smd LED [color="Yellow (585nm)" package="0603 [SMD]"]
  R5 = Resistor [tolerance=±5% resistance=220 package="1206 [SMD]"]
  R6 = Resistor [tolerance=±5% resistance=220 package="1206 [SMD]"]

nets:
  N1: Raspberry_Pi_1.GPIO17, R3.Pin_0
  N2: Raspberry_Pi_1.GPIO27, R6.Pin_0
  N3: Raspberry_Pi_1.GPIO22, R5.Pin_0
  N4: Raspberry_Pi_1.GPIO24, R1.Pin_1, R2.Pin_0
  N5: Raspberry_Pi_1.GPIO23, HC-SR04_Sensor_1.TRIG
  5V: Raspberry_Pi_1.5V, HC-SR04_Sensor_1.VCC
  N6: HC-SR04_Sensor_1.ECHO, R1.Pin_0
  N7: HC-SR04_Sensor_1.GND, R2.Pin_1, LED1.cathode, LED2.cathode, LED3.cathode
  N8: R3.Pin_1, LED1.anode
  N9: LED2.anode, R6.Pin_1
  N10: LED3.anode, R5.Pin_1
