# Fritzing sketch PIR_Sketch (saved by Fritzing 0.9.5d)
breadboards: 1

parts:
  Raspberry_Pi_1 = Raspberry Pi 3 [part_number=RPI-3-V1.2]
  PIR1 = PIR sensor
  LED1 = smd LED [color="Red (633nm)" package="1206 [SMD]"]
  R1 = Resistor [tolerance=±5% resistance=220 package="2010 [SMD]"]

nets:
  N1: Raspberry_Pi_1.GIPO23, PIR1.SIG
  N2: Raspberry_Pi_1.GIPO18, R1.Pin_0
  GND: Raspberry_Pi_1.GND, PIR1.GND, LED1.cathode
  5V: Raspberry_Pi_1.5V, PIR1.VDD
  N3: LED1.anode, R1.Pin_1
