# Fritzing sketch Exercici2 (saved by Fritzing 0.9.5d)
breadboards: 1

parts:
  Raspberry_Pi_1 = Raspberry Pi 3 [part_number=RPI-3-V1.2]
  HC-SR04_Sensor_1 = HC-SR04 Ultrasonic Distance Sensor
  R1 = Resistor [tolerance=±5% resistance=1k package="0805 [SMD]"]
  R2 = Resistor [tolerance=±5% resistance=2.2k package="2010 [SMD]"]
  buz1 = Piezo Buzzer

nets:
  N1: Raspberry_Pi_1.GPIO24, R1.Pin_1, R2.Pin_0
  N2: Raspberry_Pi_1.GPIO23, HC-SR04_Sensor_1.TRIG
  N3: Raspberry_Pi_1.GPIO18, buz1.pin_1
  5V: Raspberry_Pi_1.5V, HC-SR04_Sensor_1.VCC
  N4: HC-SR04_Sensor_1.ECHO, R1.Pin_0
  N5: HC-SR04_Sensor_1.GND, R2.Pin_1, buz1.pin_2

custom parts:
  Piezo Buzzer: Part from https://www.nutsvolts.com/magazine/article/november2012_SmileysWorkshop. Breadboard and icon images modified to be 0.3" in spacing and be more similar to the actual physical part.
