# Fritzing sketch Exercici4 (saved by Fritzing 0.9.5d)
breadboards: 1

parts:
  Raspberry_Pi_1 = Raspberry Pi 3 [part_number=RPI-3-V1.2]
  R3 = Resistor [tolerance=±5% resistance=220 package="1206 [SMD]"]
  LED1 = smd LED [color="Red (633nm)" package="0603 [SMD]"]
  PIR1 = PIR sensor
  buz1 = Piezo Buzzer  # not connected

nets:
  N1: Raspberry_Pi_1.GPIO17, R3.Pin_0
  N2: Raspberry_Pi_1.GPIO23, PIR1.SIG
  5V: Raspberry_Pi_1.5V, PIR1.VDD
  N3: R3.Pin_1, LED1.anode
  N4: LED1.cathode, PIR1.GND

custom parts:
  Piezo Buzzer: Part from https://www.nutsvolts.com/magazine/article/november2012_SmileysWorkshop. Breadboard and icon images modified to be 0.3" in spacing and be more similar to the actual physical part.
