# Fritzing sketch Esquema de montaje (saved by Fritzing 0.9.5d)
breadboards: 1

parts:
  LED1 = LED - 5mm [color="Red (633nm)" package="5 mm [THT]"]
  LED2 = LED - 5mm [color="Red (633nm)" package="5 mm [THT]"]
  R1 = Resistor [tolerance=±5% resistance=220 package=THT]
  R2 = Resistor [tolerance=±5% resistance=220 package=THT]
  Raspberry_Pi_1 = Raspberry Pi 3 [part_number=RPI-3-V1.2]

nets:
  N1: LED1.cathode, LED2.cathode, R1.Pin_0, R2.Pin_0, Raspberry_Pi_1.GND
  N2: LED1.anode, R2.Pin_1, Raspberry_Pi_1.GPIO17
  N3: LED2.anode, Raspberry_Pi_1.GPIO4
